// Digital circuit calcq.dig as structural Verilog
module calcq (
  input  [3:0] DATA,
  input  DA,
  input  CLK,
  output [3:0] D0,
  output [3:0] D1,
  output [3:0] D2,
  output [3:0] D3,
  output [3:0] D4,
  output [3:0] D5,
  output [3:0] D6,
  output [3:0] D7
);

  wire _4_bit_adder_3_c0, _4_bit_adder_5_c0, _4_bit_adder_7_c0, _4_bit_adder_9_c0, _4_bit_adder_11_c0,
       _4_bit_adder_13_c0, add_1_c_o, and_1_out, and_2_out, and_3_out, and_4_out, comparatorrr_1_gt,
       comparatorrr_2_gt, comparatorrr_3_gt, comparatorrr_4_gt, comparatorrr_5_gt, comparatorrr_6_gt,
       comparatorrr_7_gt, comparatorrr_8_gt, d_ff_1_nq, multiplexer_5_out, multiplexer_9_out,
       multiplexer_15_out, multiplexer_20_out, multiplexer_25_out, multiplexer_30_out, multiplexer_35_out,
       multiplexer_40_out, not_1_out, or_1_out;
  wire [3:0] _4_bit_adder_1_sum, _4_bit_adder_2_sum, _4_bit_adder_3_sum, _4_bit_adder_4_sum,
       _4_bit_adder_5_sum, _4_bit_adder_6_sum, _4_bit_adder_7_sum, _4_bit_adder_8_sum, _4_bit_adder_9_sum,
       _4_bit_adder_10_sum, _4_bit_adder_11_sum, _4_bit_adder_12_sum, _4_bit_adder_13_sum,
       _4_bit_adder_14_sum, _4_bit_adder_15_sum, add_1_s, driver_1_out, driver_2_out, driver_3_out,
       driver_4_out, driver_5_out, driver_6_out, driver_7_out, driver_8_out, multiplexer_1_out,
       multiplexer_2_out, multiplexer_3_out, multiplexer_6_out, multiplexer_7_out, multiplexer_8_out,
       multiplexer_11_out, multiplexer_12_out, multiplexer_13_out, multiplexer_16_out, multiplexer_17_out,
       multiplexer_18_out, multiplexer_21_out, multiplexer_22_out, multiplexer_23_out, multiplexer_26_out,
       multiplexer_27_out, multiplexer_28_out, multiplexer_31_out, multiplexer_32_out, multiplexer_33_out,
       multiplexer_36_out, multiplexer_37_out, multiplexer_38_out, register_1_q, register_2_q, register_3_q,
       register_4_q, register_5_q, register_6_q, register_7_q, register_8_q, register_9_q, register_10_q,
       register_11_q, register_12_q, register_13_q, register_14_q, register_15_q, register_16_q;

  not not_1 (not_1_out, DATA[0]);
  or or_1 (or_1_out, and_2_out, and_1_out);
  and and_1 (and_1_out, not_1_out, DATA[1], DATA[2], DATA[3]);
  and and_2 (and_2_out, DATA[0], DATA[1], DATA[2], DATA[3]);
  Multiplexer #(.Bits(4)) multiplexer_1 (.sel(or_1_out), .in_0(DATA), .in_1(4'b0000), .out(multiplexer_1_out));
  D_FF d_ff_1 (.D(DA), .C(CLK), .nQ(d_ff_1_nq));  // open: Q
  and and_3 (and_3_out, d_ff_1_nq, DA);
  and and_4 (and_4_out, and_3_out, and_2_out);
  comparatorrr comparatorrr_1 (.A(_4_bit_adder_1_sum), .B(4'b1001), .gt(comparatorrr_1_gt));  // open: eq, lt
  Register #(.Bits(4)) register_1 (.D(multiplexer_1_out), .C(CLK), .en(and_3_out), .Q(register_1_q));
  _4_bit_Adder _4_bit_adder_1 (.A(register_2_q), .B(driver_1_out), .Ci(1'b0), .Sum(_4_bit_adder_1_sum));  // open: C0
  Multiplexer #(.Bits(4)) multiplexer_2 (
    .sel(comparatorrr_1_gt), .in_0(4'b0000), .in_1(4'b0110), .out(multiplexer_2_out));
  Register #(.Bits(4)) register_2 (.D(multiplexer_3_out), .C(CLK), .en(multiplexer_5_out), .Q(register_2_q));
  Multiplexer #(.Bits(4)) multiplexer_3 (.sel(and_1_out), .in_0(add_1_s), .in_1(4'b0000), .out(multiplexer_3_out));
  assign driver_1_out = and_4_out ? register_1_q : 4'bz;  // Driver driver_1
  Multiplexer #(.Bits(4)) multiplexer_4 (.sel(and_2_out), .in_0(register_1_q), .in_1(register_2_q), .out(D0));
  Add #(.Bits(4)) add_1 (.a(multiplexer_2_out), .b(_4_bit_adder_1_sum), .c_i(1'b0), .s(add_1_s), .c_o(add_1_c_o));
  Multiplexer multiplexer_5 (.sel(and_1_out), .in_0(and_4_out), .in_1(and_1_out), .out(multiplexer_5_out));
  Multiplexer #(.Bits(4)) multiplexer_6 (.sel(or_1_out), .in_0(register_1_q), .in_1(4'b0000), .out(multiplexer_6_out));
  Register #(.Bits(4)) register_3 (.D(multiplexer_6_out), .C(CLK), .en(and_3_out), .Q(register_3_q));
  comparatorrr comparatorrr_2 (.A(_4_bit_adder_2_sum), .B(4'b1001), .gt(comparatorrr_2_gt));  // open: eq, lt
  Register #(.Bits(4)) register_4 (.D(multiplexer_7_out), .C(CLK), .en(multiplexer_9_out), .Q(register_4_q));
  Multiplexer #(.Bits(4)) multiplexer_7 (
    .sel(and_1_out), .in_0(_4_bit_adder_3_sum), .in_1(4'b0000), .out(multiplexer_7_out));
  assign driver_2_out = and_4_out ? register_3_q : 4'bz;  // Driver driver_2
  _4_bit_Adder _4_bit_adder_2 (
    .A(register_4_q), .B(driver_2_out), .Ci(add_1_c_o), .Sum(_4_bit_adder_2_sum));  // open: C0
  Multiplexer #(.Bits(4)) multiplexer_8 (
    .sel(comparatorrr_2_gt), .in_0(4'b0000), .in_1(4'b0110), .out(multiplexer_8_out));
  Multiplexer multiplexer_9 (.sel(and_1_out), .in_0(and_4_out), .in_1(and_1_out), .out(multiplexer_9_out));
  _4_bit_Adder _4_bit_adder_3 (
    .A(multiplexer_8_out), .B(_4_bit_adder_2_sum), .Ci(1'b0), .Sum(_4_bit_adder_3_sum), .C0(_4_bit_adder_3_c0));
  Multiplexer #(.Bits(4)) multiplexer_10 (.sel(and_2_out), .in_0(register_3_q), .in_1(register_4_q), .out(D1));
  Multiplexer #(.Bits(4)) multiplexer_11 (
    .sel(or_1_out), .in_0(register_3_q), .in_1(4'b0000), .out(multiplexer_11_out));
  Register #(.Bits(4)) register_5 (.D(multiplexer_11_out), .C(CLK), .en(and_3_out), .Q(register_5_q));
  comparatorrr comparatorrr_3 (.A(_4_bit_adder_4_sum), .B(4'b1001), .gt(comparatorrr_3_gt));  // open: eq, lt
  Register #(.Bits(4)) register_6 (.D(multiplexer_12_out), .C(CLK), .en(multiplexer_15_out), .Q(register_6_q));
  Multiplexer #(.Bits(4)) multiplexer_12 (
    .sel(and_1_out), .in_0(_4_bit_adder_5_sum), .in_1(4'b0000), .out(multiplexer_12_out));
  Multiplexer #(.Bits(4)) multiplexer_13 (
    .sel(comparatorrr_3_gt), .in_0(4'b0000), .in_1(4'b0110), .out(multiplexer_13_out));
  Multiplexer #(.Bits(4)) multiplexer_14 (.sel(and_2_out), .in_0(register_5_q), .in_1(register_6_q), .out(D2));
  assign driver_3_out = and_4_out ? register_5_q : 4'bz;  // Driver driver_3
  _4_bit_Adder _4_bit_adder_4 (
    .A(register_6_q), .B(driver_3_out), .Ci(_4_bit_adder_3_c0), .Sum(_4_bit_adder_4_sum));  // open: C0
  _4_bit_Adder _4_bit_adder_5 (
    .A(multiplexer_13_out), .B(_4_bit_adder_4_sum), .Ci(1'b0), .Sum(_4_bit_adder_5_sum),
    .C0(_4_bit_adder_5_c0));
  Multiplexer multiplexer_15 (.sel(and_1_out), .in_0(and_4_out), .in_1(and_1_out), .out(multiplexer_15_out));
  Multiplexer #(.Bits(4)) multiplexer_16 (
    .sel(or_1_out), .in_0(register_5_q), .in_1(4'b0000), .out(multiplexer_16_out));
  comparatorrr comparatorrr_4 (.A(_4_bit_adder_6_sum), .B(4'b1001), .gt(comparatorrr_4_gt));  // open: eq, lt
  Register #(.Bits(4)) register_7 (.D(multiplexer_16_out), .C(CLK), .en(and_3_out), .Q(register_7_q));
  Multiplexer #(.Bits(4)) multiplexer_17 (
    .sel(comparatorrr_4_gt), .in_0(4'b0000), .in_1(4'b0110), .out(multiplexer_17_out));
  Register #(.Bits(4)) register_8 (.D(multiplexer_18_out), .C(CLK), .en(multiplexer_20_out), .Q(register_8_q));
  Multiplexer #(.Bits(4)) multiplexer_18 (
    .sel(and_1_out), .in_0(_4_bit_adder_7_sum), .in_1(4'b0000), .out(multiplexer_18_out));
  Multiplexer #(.Bits(4)) multiplexer_19 (.sel(and_2_out), .in_0(register_7_q), .in_1(register_8_q), .out(D3));
  assign driver_4_out = and_4_out ? register_7_q : 4'bz;  // Driver driver_4
  _4_bit_Adder _4_bit_adder_6 (
    .A(register_8_q), .B(driver_4_out), .Ci(_4_bit_adder_5_c0), .Sum(_4_bit_adder_6_sum));  // open: C0
  _4_bit_Adder _4_bit_adder_7 (
    .A(multiplexer_17_out), .B(_4_bit_adder_6_sum), .Ci(1'b0), .Sum(_4_bit_adder_7_sum),
    .C0(_4_bit_adder_7_c0));
  Multiplexer multiplexer_20 (.sel(and_1_out), .in_0(and_4_out), .in_1(and_1_out), .out(multiplexer_20_out));
  Multiplexer #(.Bits(4)) multiplexer_21 (
    .sel(or_1_out), .in_0(register_7_q), .in_1(4'b0000), .out(multiplexer_21_out));
  Register #(.Bits(4)) register_9 (.D(multiplexer_21_out), .C(CLK), .en(and_3_out), .Q(register_9_q));
  comparatorrr comparatorrr_5 (.A(_4_bit_adder_8_sum), .B(4'b1001), .gt(comparatorrr_5_gt));  // open: eq, lt
  Multiplexer #(.Bits(4)) multiplexer_22 (
    .sel(comparatorrr_5_gt), .in_0(4'b0000), .in_1(4'b0110), .out(multiplexer_22_out));
  Register #(.Bits(4)) register_10 (.D(multiplexer_23_out), .C(CLK), .en(multiplexer_25_out), .Q(register_10_q));
  Multiplexer #(.Bits(4)) multiplexer_23 (
    .sel(and_1_out), .in_0(_4_bit_adder_9_sum), .in_1(4'b0000), .out(multiplexer_23_out));
  Multiplexer #(.Bits(4)) multiplexer_24 (.sel(and_2_out), .in_0(register_9_q), .in_1(register_10_q), .out(D4));
  assign driver_5_out = and_4_out ? register_9_q : 4'bz;  // Driver driver_5
  _4_bit_Adder _4_bit_adder_8 (
    .A(register_10_q), .B(driver_5_out), .Ci(_4_bit_adder_7_c0), .Sum(_4_bit_adder_8_sum));  // open: C0
  _4_bit_Adder _4_bit_adder_9 (
    .A(multiplexer_22_out), .B(_4_bit_adder_8_sum), .Ci(1'b0), .Sum(_4_bit_adder_9_sum),
    .C0(_4_bit_adder_9_c0));
  Multiplexer multiplexer_25 (.sel(and_1_out), .in_0(and_4_out), .in_1(and_1_out), .out(multiplexer_25_out));
  Multiplexer #(.Bits(4)) multiplexer_26 (
    .sel(or_1_out), .in_0(register_9_q), .in_1(4'b0000), .out(multiplexer_26_out));
  Register #(.Bits(4)) register_11 (.D(multiplexer_26_out), .C(CLK), .en(and_3_out), .Q(register_11_q));
  comparatorrr comparatorrr_6 (.A(_4_bit_adder_10_sum), .B(4'b1001), .gt(comparatorrr_6_gt));  // open: eq, lt
  Multiplexer #(.Bits(4)) multiplexer_27 (
    .sel(comparatorrr_6_gt), .in_0(4'b0000), .in_1(4'b0110), .out(multiplexer_27_out));
  Register #(.Bits(4)) register_12 (.D(multiplexer_28_out), .C(CLK), .en(multiplexer_30_out), .Q(register_12_q));
  assign driver_6_out = and_4_out ? register_11_q : 4'bz;  // Driver driver_6
  _4_bit_Adder _4_bit_adder_10 (
    .A(register_12_q), .B(driver_6_out), .Ci(_4_bit_adder_9_c0), .Sum(_4_bit_adder_10_sum));  // open: C0
  Multiplexer #(.Bits(4)) multiplexer_28 (
    .sel(and_1_out), .in_0(_4_bit_adder_11_sum), .in_1(4'b0000), .out(multiplexer_28_out));
  Multiplexer #(.Bits(4)) multiplexer_29 (.sel(and_2_out), .in_0(register_11_q), .in_1(register_12_q), .out(D5));
  _4_bit_Adder _4_bit_adder_11 (
    .A(multiplexer_27_out), .B(_4_bit_adder_10_sum), .Ci(1'b0), .Sum(_4_bit_adder_11_sum),
    .C0(_4_bit_adder_11_c0));
  Multiplexer multiplexer_30 (.sel(and_1_out), .in_0(and_4_out), .in_1(and_1_out), .out(multiplexer_30_out));
  Multiplexer #(.Bits(4)) multiplexer_31 (
    .sel(or_1_out), .in_0(register_11_q), .in_1(4'b0000), .out(multiplexer_31_out));
  Register #(.Bits(4)) register_13 (.D(multiplexer_31_out), .C(CLK), .en(and_3_out), .Q(register_13_q));
  comparatorrr comparatorrr_7 (.A(_4_bit_adder_12_sum), .B(4'b1001), .gt(comparatorrr_7_gt));  // open: eq, lt
  Register #(.Bits(4)) register_14 (.D(multiplexer_33_out), .C(CLK), .en(multiplexer_35_out), .Q(register_14_q));
  assign driver_7_out = and_4_out ? register_13_q : 4'bz;  // Driver driver_7
  _4_bit_Adder _4_bit_adder_12 (
    .A(register_14_q), .B(driver_7_out), .Ci(_4_bit_adder_11_c0), .Sum(_4_bit_adder_12_sum));  // open: C0
  Multiplexer #(.Bits(4)) multiplexer_32 (
    .sel(comparatorrr_7_gt), .in_0(4'b0000), .in_1(4'b0110), .out(multiplexer_32_out));
  Multiplexer #(.Bits(4)) multiplexer_33 (
    .sel(and_1_out), .in_0(_4_bit_adder_13_sum), .in_1(4'b0000), .out(multiplexer_33_out));
  Multiplexer #(.Bits(4)) multiplexer_34 (.sel(and_2_out), .in_0(register_13_q), .in_1(register_14_q), .out(D6));
  _4_bit_Adder _4_bit_adder_13 (
    .A(multiplexer_32_out), .B(_4_bit_adder_12_sum), .Ci(1'b0), .Sum(_4_bit_adder_13_sum),
    .C0(_4_bit_adder_13_c0));
  Multiplexer multiplexer_35 (.sel(and_1_out), .in_0(and_4_out), .in_1(and_1_out), .out(multiplexer_35_out));
  Multiplexer #(.Bits(4)) multiplexer_36 (
    .sel(or_1_out), .in_0(register_13_q), .in_1(4'b0000), .out(multiplexer_36_out));
  Register #(.Bits(4)) register_15 (.D(multiplexer_36_out), .C(CLK), .en(and_3_out), .Q(register_15_q));
  comparatorrr comparatorrr_8 (.A(_4_bit_adder_14_sum), .B(4'b1001), .gt(comparatorrr_8_gt));  // open: eq, lt
  Multiplexer #(.Bits(4)) multiplexer_37 (
    .sel(comparatorrr_8_gt), .in_0(4'b0000), .in_1(4'b0110), .out(multiplexer_37_out));
  Register #(.Bits(4)) register_16 (.D(multiplexer_38_out), .C(CLK), .en(multiplexer_40_out), .Q(register_16_q));
  Multiplexer #(.Bits(4)) multiplexer_38 (
    .sel(and_1_out), .in_0(_4_bit_adder_15_sum), .in_1(4'b0000), .out(multiplexer_38_out));
  Multiplexer #(.Bits(4)) multiplexer_39 (.sel(and_2_out), .in_0(register_15_q), .in_1(register_16_q), .out(D7));
  assign driver_8_out = and_4_out ? register_15_q : 4'bz;  // Driver driver_8
  _4_bit_Adder _4_bit_adder_14 (
    .A(register_16_q), .B(driver_8_out), .Ci(_4_bit_adder_13_c0), .Sum(_4_bit_adder_14_sum));  // open: C0
  _4_bit_Adder _4_bit_adder_15 (
    .A(multiplexer_37_out), .B(_4_bit_adder_14_sum), .Ci(1'b0), .Sum(_4_bit_adder_15_sum));  // open: C0
  Multiplexer multiplexer_40 (.sel(and_1_out), .in_0(and_4_out), .in_1(and_1_out), .out(multiplexer_40_out));
endmodule
