// Digital circuit comparatorrr.dig as structural Verilog
module comparatorrr (
  input  [3:0] A,
  input  [3:0] B,
  output gt,
  output eq,
  output lt
);

  wire and_1_out, and_2_out, and_3_out, and_4_out, and_5_out, and_6_out, and_7_out, not_1_out, not_2_out,
       not_3_out, not_4_out, xnor_1_out, xnor_2_out, xnor_3_out, xnor_4_out;

  not not_1 (not_1_out, B[3]);
  not not_2 (not_2_out, B[2]);
  not not_3 (not_3_out, B[1]);
  not not_4 (not_4_out, B[0]);
  xnor xnor_1 (xnor_1_out, A[3], B[3]);
  and and_1 (and_1_out, A[3], not_1_out);
  xnor xnor_2 (xnor_2_out, A[2], B[2]);
  and and_2 (and_2_out, A[2], not_2_out);
  xnor xnor_3 (xnor_3_out, A[1], B[1]);
  and and_3 (and_3_out, A[1], not_3_out);
  xnor xnor_4 (xnor_4_out, A[0], B[0]);
  and and_4 (and_4_out, A[0], not_4_out);
  and and_5 (and_5_out, xnor_1_out, and_2_out);
  and and_6 (and_6_out, xnor_1_out, xnor_2_out, and_3_out);
  and and_7 (and_7_out, xnor_1_out, xnor_2_out, xnor_3_out, and_4_out);
  and and_8 (eq, xnor_1_out, xnor_2_out, xnor_4_out, xnor_3_out);
  or or_1 (gt, and_1_out, and_5_out, and_6_out, and_7_out);
  nor nor_1 (lt, eq, gt);
endmodule
